# Fritzing sketch Car (saved by Fritzing 0.9.4)

parts:
  L298N1 = L298N DC motor driver
  元件1 = Arduino Mega 2560 (Rev3)
  L298N2 = L298N DC motor driver
  元件2 = Bluetooth HC-05 Macho
  J1 = Basic Servo
  M1 = 5-ir-array-sensor [package=THT]
  VCC1 = Battery block 9V
  HC-SR04_Sensor_1 = HC-SR04 Ultrasonic Distance Sensor
  M2 = DC Motor  # not connected
  M3 = DC Motor  # not connected
  M4 = DC Motor  # not connected
  M5 = DC Motor  # not connected

nets:
  12V: L298N1.12V, L298N2.12V, VCC1.+
  GND: L298N1.GND, L298N2.GND, VCC1.-
  5V: L298N1.5V, 元件1.5V, L298N2.5V, HC-SR04_Sensor_1.VCC
  N1: L298N1.ENA, L298N1.IN1, 元件1.D29
  N2: L298N1.IN2, 元件1.D31
  N3: L298N1.IN3, 元件1.D33
  N4: L298N1.IN4, 元件1.D27
  N5: 元件1.A0, M1.S5
  N6: 元件1.A1, M1.S4
  N7: 元件1.A2, M1.S3
  N8: 元件1.A3, M1.S2
  N9: 元件1.A4, M1.S1
  N10: 元件1.D15/RX3, 元件2.TXD
  N11: 元件1.D14/TX3, 元件2.RXD
  GND_2: 元件1.GND, HC-SR04_Sensor_1.GND
  N12: 元件1.D22, HC-SR04_Sensor_1.ECHO
  N13: 元件1.D23, J1.pulse
  N14: 元件1.D25, HC-SR04_Sensor_1.TRIG
  N15: 元件1.D35, L298N2.IN4
  N16: 元件1.D37, L298N2.ENA, L298N2.IN1
  N17: 元件1.D39, L298N2.IN2
  N18: 元件1.D41, L298N2.IN3
  GND_3: J1.gnd, M1.GND
  VCC: J1.vcc, M1.VCC

custom parts:
  L298N DC motor driver: 2x DC motor driver with 78M05 positive voltage regulator (7..35 V) L298N: max 46 V, 2 A Set 5 V Enable jumper to enable 5 V regultor (needed for the L298N) and +5 V output at screw terminal or supply external +5 V at screw terminal Set ENA and/or ENB to +5 V to enable motor permanently or supply ENA and/or ENB with PWM signal IN1 and IN2 set rotation directory for motor A (OUT1/OUT2) IN2 and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
  5-ir-array-sensor: 5 IR array sensor.
